# Fritzing sketch LaserHarp (saved by Fritzing 0.9.3b)
breadboards: 1

parts:
  Teensy1 = Teensy 2.0
  R1 = Resistor [tolerance=±5% resistance=1k package=THT]
  LED1 = LED - 5mm [color="Red (633nm)" package="5 mm [THT]"]
  U1 = MCP4725 [package=SOT23-6]
  U2 = MCP4725 [package=SOT23-6]
  U3 = LM124-324 Quad Opamp [package="DIP (Dual Inline)"]
  R4 = Resistor [tolerance=±5% resistance=22k package=THT]
  R5 = Resistor [tolerance=±5% resistance=22k package=THT]
  R6 = Resistor [tolerance=±5% resistance=22k package=THT]
  R7 = Resistor [tolerance=±5% resistance=22k package=THT]
  JP1 = Header 3 [package=screwterminal-3.5mm-3_lock.007s]
  JP3 = Header 4 [package=molex-1x4_lock]
  JP4 = Header 4 [package=molex-1x4_lock]
  R8 = Rotary Potentiometer (Small) [maximum_resistance=10kΩ package=THT]
  Q1 = LTR-301 [package=ltr-301]
  R9 = Resistor [tolerance=±5% resistance=68 package=THT]
  R10 = Resistor [tolerance=±5% resistance=68 package=THT]
  R11 = Resistor [tolerance=±5% resistance=68 package=THT]
  R12 = Resistor [tolerance=±5% resistance=68 package=THT]
  IC1 = Dual Op-Amp [package=dip08]
  R13 = Resistor [tolerance=±5% resistance=10k package=THT]
  R14 = Resistor [tolerance=±5% resistance=10k package=THT]
  R15 = Resistor [tolerance=±5% resistance=10k package=THT]
  R16 = Resistor [tolerance=±5% resistance=10k package=THT]
  R17 = Resistor [tolerance=±5% resistance=1k package=THT]
  J1 = Dagu DGServo 9g header (male) [package=THT]
  R18 = Resistor [tolerance=±5% resistance=470 package=THT]
  R19 = Resistor [tolerance=±5% resistance=470 package=THT]

nets:
  VSS: Teensy1.GND, LED1.anode, U1.VSS, U1.AO, U2.VSS, U3.2IN+, U3.3IN+, JP1.2, R8.leg1, J1.pulse
  N1: Teensy1.B7, JP4.3
  N2: Teensy1.D0, U1.SCL, U2.SCL, R19.Pin_1
  N3: Teensy1.D1, U1.SDA, U2.SDA, R18.Pin_1
  N4: Teensy1.C6, JP4.2
  N5: Teensy1.C7, JP4.1
  N6: Teensy1.D7, R1.Pin_0, R17.Pin_0
  N7: Teensy1.B5, R8.wiper, Q1.E
  VDD: Teensy1.VCC, U1.VDD, U2.VDD, U2.AO, R14.Pin_0, R16.Pin_1, R18.Pin_0, R19.Pin_0
  N8: R1.Pin_1, LED1.cathode
  N9: U1.VOUT, IC1.A_+IN
  N10: U2.VOUT, IC1.B_+IN
  N11: U3.1OUT, U3.1IN-, R4.Pin_0, R9.Pin_0
  N12: U3.1IN+, IC1.A_OUT, R15.Pin_0
  N13: U3.VCC+, JP1.3, IC1.A_V+
  N14: U3.2IN-, R4.Pin_1, R5.Pin_0
  N15: U3.2OUT, R5.Pin_1, R10.Pin_0
  N16: U3.3OUT, R6.Pin_1, R12.Pin_0
  N17: U3.3IN-, R6.Pin_0, R7.Pin_1
  N18: U3.VCC-, JP1.1, IC1.A_V-
  N19: U3.4IN+, IC1.B_OUT, R13.Pin_0
  N20: U3.4IN-, U3.4OUT, R7.Pin_0, R11.Pin_0
  N21: JP3.1, R10.Pin_1
  N22: JP3.2, R9.Pin_1
  N23: JP3.3, R12.Pin_1
  N24: JP3.4, R11.Pin_1
  N25: IC1.A_-IN, R15.Pin_1, R16.Pin_0
  N26: IC1.B_-IN, R13.Pin_1, R14.Pin_1
